// Logisim project BlacknWhite_circuit.circ as structural Verilog: 8 circuits, main circuit main
module main (
);

  wire and_1_out, button_1_out, button_2_out, button_3_out, button_4_out, button_5_out, button_6_out,
       button_7_out, button_8_out, button_9_out, button_10_out, button_11_out, button_12_out, button_13_out,
       button_14_out, button_15_out, button_16_out, button_17_out, button_18_out, clock_1_out, REGAME_out,
       RESET2_out, RESET_out, RESULT_out, rgb_video_1_p1, rgb_video_1_p2;
  wire [3:0] pla_1_out, pla_2_out, R, SC1, SC2;
  wire [4:0] coveroutput_1_out_2, coveroutput_1_out_3, coveroutput_1_out_4, coveroutput_2_out_2,
       coveroutput_2_out_3, coveroutput_2_out_4;
  wire [6:0] alladder_1_out_10, alladder_1_out_11, alladder_1_out_12, alladder_1_out_13, alladder_1_out_14,
       alladder_1_out_15, alladder_1_out_16, alladder_1_out_17, alladder_1_out_18, alladder_2_out_10,
       alladder_2_out_11, alladder_2_out_12, alladder_2_out_13, alladder_2_out_14, alladder_2_out_15,
       alladder_2_out_16, alladder_2_out_17, alladder_2_out_18, CA1, CA2, CA3, CA4, CA5, CA6, CA7, CA8, CA9,
       CD1, CD2, CD3, CD4, CD5, CD6, CD7, CD8, CD9, end9r_1_out_6, end9r_1_out_7, end9r_1_out_8,
       end9r_1_out_9, end9r_1_out_10, end9r_1_out_11, end9r_1_out_12, end9r_1_out_13, end9r_1_out_14,
       ledoutput_1_out_2, ledoutput_1_out_3, ledoutput_1_out_4, ledoutput_1_out_5, ledoutput_1_out_6,
       ledoutput_2_out_2, ledoutput_2_out_3, ledoutput_2_out_4, ledoutput_2_out_5, ledoutput_2_out_6,
       ledoutput_3_out_2, ledoutput_3_out_3, ledoutput_3_out_4, ledoutput_3_out_5, ledoutput_3_out_6,
       ledoutput_4_out_2, ledoutput_4_out_3, ledoutput_4_out_4, ledoutput_4_out_5, ledoutput_4_out_6,
       ledoutput_5_out_2, ledoutput_5_out_3, ledoutput_5_out_4, ledoutput_5_out_5, ledoutput_5_out_6,
       ledoutput_6_out_2, ledoutput_6_out_3, ledoutput_6_out_4, ledoutput_6_out_5, ledoutput_6_out_6,
       ledoutput_7_out_2, ledoutput_7_out_3, ledoutput_7_out_4, ledoutput_7_out_5, ledoutput_7_out_6,
       ledoutput_8_out_2, ledoutput_8_out_3, ledoutput_8_out_4, ledoutput_8_out_5, ledoutput_8_out_6,
       ledoutput_9_out_2, ledoutput_9_out_3, ledoutput_9_out_4, ledoutput_9_out_5, ledoutput_9_out_6,
       ledoutput_10_out_2, ledoutput_10_out_3, ledoutput_10_out_4, ledoutput_10_out_5, ledoutput_10_out_6,
       ledoutput_11_out_2, ledoutput_11_out_3, ledoutput_11_out_4, ledoutput_11_out_5, ledoutput_11_out_6,
       ledoutput_12_out_2, ledoutput_12_out_3, ledoutput_12_out_4, ledoutput_12_out_5, ledoutput_12_out_6,
       ledoutput_13_out_2, ledoutput_13_out_3, ledoutput_13_out_4, ledoutput_13_out_5, ledoutput_13_out_6,
       ledoutput_14_out_2, ledoutput_14_out_3, ledoutput_14_out_4, ledoutput_14_out_5, ledoutput_14_out_6,
       ledoutput_15_out_2, ledoutput_15_out_3, ledoutput_15_out_4, ledoutput_15_out_5, ledoutput_15_out_6,
       ledoutput_16_out_2, ledoutput_16_out_3, ledoutput_16_out_4, ledoutput_16_out_5, ledoutput_16_out_6,
       ledoutput_17_out_2, ledoutput_17_out_3, ledoutput_17_out_4, ledoutput_17_out_5, ledoutput_17_out_6,
       ledoutput_18_out_2, ledoutput_18_out_3, ledoutput_18_out_4, ledoutput_18_out_5, ledoutput_18_out_6,
       ledoutput_19_out_2, ledoutput_19_out_3, ledoutput_19_out_4, ledoutput_19_out_5, ledoutput_19_out_6,
       ledoutput_20_out_2, ledoutput_20_out_3, ledoutput_20_out_4, ledoutput_20_out_5, ledoutput_20_out_6,
       P1, P1S, P2, P2S;
  wire [7:0] rgb_video_1_p3, rgb_video_1_p4;
  wire [15:0] rgb_video_1_p5;

  Keyboard #(.buflen(1)) keyboard_1 (.clr(button_2_out), .data(CD1));  // open: clk, re, avail
  Keyboard #(.buflen(1)) keyboard_2 (.clr(button_1_out), .data(CA1));  // open: clk, re, avail
  Button button_1 (.out(button_1_out));
  DotMatrix dotmatrix_1 (
    .col0(ledoutput_1_out_2), .col1(ledoutput_1_out_3), .col2(ledoutput_1_out_4), .col3(ledoutput_1_out_5),
    .col4(ledoutput_1_out_6));
  LEDoutput ledoutput_1 (
    .out_2(ledoutput_1_out_2), .out_3(ledoutput_1_out_3), .out_4(ledoutput_1_out_4),
    .out_5(ledoutput_1_out_5), .out_6(ledoutput_1_out_6), .in_1(CA1));
  DotMatrix dotmatrix_2 (
    .col0(ledoutput_2_out_2), .col1(ledoutput_2_out_3), .col2(ledoutput_2_out_4), .col3(ledoutput_2_out_5),
    .col4(ledoutput_2_out_6));
  LEDoutput ledoutput_2 (
    .out_2(ledoutput_2_out_2), .out_3(ledoutput_2_out_3), .out_4(ledoutput_2_out_4),
    .out_5(ledoutput_2_out_5), .out_6(ledoutput_2_out_6), .in_1(CD1));
  Button button_2 (.out(button_2_out));
  DotMatrix #(.matrixcols(40), .matrixrows(38)) dotmatrix_3 ();  // open: col0, col1, col2, col3, col4, col5, col6, col7, col8, col9, col10, col11, col12, col13, col14, col15, col16, col17, col18, col19, col20, col21, col22, col23, col24, col25, col26, col27, col28, col29, col30, col31, col32, col33, col34, col35, col36, col37, col38, col39
  Keyboard #(.buflen(1)) keyboard_3 (.clr(button_4_out), .data(CD2));  // open: clk, re, avail
  Keyboard #(.buflen(1)) keyboard_4 (.clr(button_3_out), .data(CA2));  // open: clk, re, avail
  Button button_3 (.out(button_3_out));
  DotMatrix dotmatrix_4 (
    .col0(ledoutput_3_out_2), .col1(ledoutput_3_out_3), .col2(ledoutput_3_out_4), .col3(ledoutput_3_out_5),
    .col4(ledoutput_3_out_6));
  LEDoutput ledoutput_3 (
    .out_2(ledoutput_3_out_2), .out_3(ledoutput_3_out_3), .out_4(ledoutput_3_out_4),
    .out_5(ledoutput_3_out_5), .out_6(ledoutput_3_out_6), .in_1(CA2));
  DotMatrix #(.matrixcols(3), .matrixrows(5)) dotmatrix_5 (
    .col0(coveroutput_1_out_2), .col1(coveroutput_1_out_3), .col2(coveroutput_1_out_4));
  COVERoutput coveroutput_1 (
    .out_2(coveroutput_1_out_2), .out_3(coveroutput_1_out_3), .out_4(coveroutput_1_out_4), .in_1(P2));
  DotMatrix dotmatrix_6 (
    .col0(ledoutput_4_out_2), .col1(ledoutput_4_out_3), .col2(ledoutput_4_out_4), .col3(ledoutput_4_out_5),
    .col4(ledoutput_4_out_6));
  LEDoutput ledoutput_4 (
    .out_2(ledoutput_4_out_2), .out_3(ledoutput_4_out_3), .out_4(ledoutput_4_out_4),
    .out_5(ledoutput_4_out_5), .out_6(ledoutput_4_out_6), .in_1(P2));
  DotMatrix #(.matrixcols(3), .matrixrows(5)) dotmatrix_7 (
    .col0(coveroutput_2_out_2), .col1(coveroutput_2_out_3), .col2(coveroutput_2_out_4));
  COVERoutput coveroutput_2 (
    .out_2(coveroutput_2_out_2), .out_3(coveroutput_2_out_3), .out_4(coveroutput_2_out_4), .in_1(P1));
  DotMatrix dotmatrix_8 (
    .col0(ledoutput_5_out_2), .col1(ledoutput_5_out_3), .col2(ledoutput_5_out_4), .col3(ledoutput_5_out_5),
    .col4(ledoutput_5_out_6));
  LEDoutput ledoutput_5 (
    .out_2(ledoutput_5_out_2), .out_3(ledoutput_5_out_3), .out_4(ledoutput_5_out_4),
    .out_5(ledoutput_5_out_5), .out_6(ledoutput_5_out_6), .in_1(P1));
  DotMatrix dotmatrix_9 (
    .col0(ledoutput_6_out_2), .col1(ledoutput_6_out_3), .col2(ledoutput_6_out_4), .col3(ledoutput_6_out_5),
    .col4(ledoutput_6_out_6));
  LEDoutput ledoutput_6 (
    .out_2(ledoutput_6_out_2), .out_3(ledoutput_6_out_3), .out_4(ledoutput_6_out_4),
    .out_5(ledoutput_6_out_5), .out_6(ledoutput_6_out_6), .in_1(CD2));
  Button button_4 (.out(button_4_out));
  Keyboard #(.buflen(1)) keyboard_5 (.clr(button_6_out), .data(CD3));  // open: clk, re, avail
  Keyboard #(.buflen(1)) keyboard_6 (.clr(button_5_out), .data(CA3));  // open: clk, re, avail
  Button button_5 (.out(button_5_out));
  DotMatrix dotmatrix_10 (
    .col0(ledoutput_7_out_2), .col1(ledoutput_7_out_3), .col2(ledoutput_7_out_4), .col3(ledoutput_7_out_5),
    .col4(ledoutput_7_out_6));
  LEDoutput ledoutput_7 (
    .out_2(ledoutput_7_out_2), .out_3(ledoutput_7_out_3), .out_4(ledoutput_7_out_4),
    .out_5(ledoutput_7_out_5), .out_6(ledoutput_7_out_6), .in_1(CA3));
  Hex_Digit_Display hex_digit_display_1 (.value(R));  // open: dp
  Hex_Digit_Display hex_digit_display_2 (.value(SC1));  // open: dp
  DotMatrix dotmatrix_11 (
    .col0(ledoutput_8_out_2), .col1(ledoutput_8_out_3), .col2(ledoutput_8_out_4), .col3(ledoutput_8_out_5),
    .col4(ledoutput_8_out_6));
  LEDoutput ledoutput_8 (
    .out_2(ledoutput_8_out_2), .out_3(ledoutput_8_out_3), .out_4(ledoutput_8_out_4),
    .out_5(ledoutput_8_out_5), .out_6(ledoutput_8_out_6), .in_1(CD3));
  Button button_6 (.out(button_6_out));
  Hex_Digit_Display hex_digit_display_3 (.value(SC2));  // open: dp
  Keyboard #(.buflen(1)) keyboard_7 (.clr(button_8_out), .data(CD4));  // open: clk, re, avail
  DotMatrix #(.matrixcols(9)) dotmatrix_12 (
    .col0(alladder_1_out_10), .col1(alladder_1_out_11), .col2(alladder_1_out_12), .col3(alladder_1_out_13),
    .col4(alladder_1_out_14), .col5(alladder_1_out_15), .col6(alladder_1_out_16), .col7(alladder_1_out_17),
    .col8(alladder_1_out_18));
  Alladder alladder_1 (
    .in_1(CA1), .in_2(CA2), .in_3(CA3), .in_4(CA4), .in_5(CA5), .in_6(CA6), .in_7(CA7), .in_8(CA8),
    .in_9(CA9), .out_10(alladder_1_out_10), .out_11(alladder_1_out_11), .out_12(alladder_1_out_12),
    .out_13(alladder_1_out_13), .out_14(alladder_1_out_14), .out_15(alladder_1_out_15),
    .out_16(alladder_1_out_16), .out_17(alladder_1_out_17), .out_18(alladder_1_out_18));
  Keyboard #(.buflen(1)) keyboard_8 (.clr(button_7_out), .data(CA4));  // open: clk, re, avail
  Button button_7 (.out(button_7_out));
  DotMatrix dotmatrix_13 (
    .col0(ledoutput_9_out_2), .col1(ledoutput_9_out_3), .col2(ledoutput_9_out_4), .col3(ledoutput_9_out_5),
    .col4(ledoutput_9_out_6));
  LEDoutput ledoutput_9 (
    .out_2(ledoutput_9_out_2), .out_3(ledoutput_9_out_3), .out_4(ledoutput_9_out_4),
    .out_5(ledoutput_9_out_5), .out_6(ledoutput_9_out_6), .in_1(CA4));
  DotMatrix dotmatrix_14 (
    .col0(ledoutput_10_out_2), .col1(ledoutput_10_out_3), .col2(ledoutput_10_out_4),
    .col3(ledoutput_10_out_5), .col4(ledoutput_10_out_6));
  LEDoutput ledoutput_10 (
    .out_2(ledoutput_10_out_2), .out_3(ledoutput_10_out_3), .out_4(ledoutput_10_out_4),
    .out_5(ledoutput_10_out_5), .out_6(ledoutput_10_out_6), .in_1(CD4));
  Button button_8 (.out(button_8_out));
  DotMatrix #(.matrixcols(9)) dotmatrix_15 (
    .col0(alladder_2_out_10), .col1(alladder_2_out_11), .col2(alladder_2_out_12), .col3(alladder_2_out_13),
    .col4(alladder_2_out_14), .col5(alladder_2_out_15), .col6(alladder_2_out_16), .col7(alladder_2_out_17),
    .col8(alladder_2_out_18));
  Alladder alladder_2 (
    .in_1(CD1), .in_2(CD2), .in_3(CD3), .in_4(CD4), .in_5(CD5), .in_6(CD6), .in_7(CD7), .in_8(CD8),
    .in_9(CD9), .out_10(alladder_2_out_10), .out_11(alladder_2_out_11), .out_12(alladder_2_out_12),
    .out_13(alladder_2_out_13), .out_14(alladder_2_out_14), .out_15(alladder_2_out_15),
    .out_16(alladder_2_out_16), .out_17(alladder_2_out_17), .out_18(alladder_2_out_18));
  Keyboard #(.buflen(1)) keyboard_9 (.clr(RESET2_out), .data(P2S));  // open: clk, re, avail
  PLA #(.in_width(7), .out_width(4), .\table ("0110001 0001 # 1번\n0110010 0010 # 2번\n0110011 0011 # 3번\n0110100 0100 # 4번\n0110101 0101 # 5번\n0110110 0110 # 6번\n0110111 0111 # 7번\n0111000 1000 # 8번\n0111001 1001 # 9번")) pla_1 (
    .in(P2S), .out(pla_1_out));
  Button REGAME (.out(REGAME_out));
  Button RESULT (.out(RESULT_out));
  PLA #(.in_width(7), .out_width(4), .\table ("0110001 0001 # 1번\n0110010 0010 # 2번\n0110011 0011 # 3번\n0110100 0100 # 4번\n0110101 0101 # 5번\n0110110 0110 # 6번\n0110111 0111 # 7번\n0111000 1000 # 8번\n0111001 1001 # 9번")) pla_2 (
    .in(P1S), .out(pla_2_out));
  Keyboard #(.buflen(1)) keyboard_10 (.clr(button_10_out), .data(CD5));  // open: clk, re, avail
  Keyboard #(.buflen(1)) keyboard_11 (.clr(RESET_out), .data(P1S));  // open: clk, re, avail
  Button RESET2 (.out(RESET2_out));
  Keyboard #(.buflen(1)) keyboard_12 (.clr(button_9_out), .data(CA5));  // open: clk, re, avail
  Button button_9 (.out(button_9_out));
  DotMatrix dotmatrix_16 (
    .col0(ledoutput_11_out_2), .col1(ledoutput_11_out_3), .col2(ledoutput_11_out_4),
    .col3(ledoutput_11_out_5), .col4(ledoutput_11_out_6));
  LEDoutput ledoutput_11 (
    .out_2(ledoutput_11_out_2), .out_3(ledoutput_11_out_3), .out_4(ledoutput_11_out_4),
    .out_5(ledoutput_11_out_5), .out_6(ledoutput_11_out_6), .in_1(CA5));
  Multiplexer #(.select(4), .width(7)) multiplexer_1 (
    .in1(CA1), .in2(CA2), .in3(CA3), .in4(CA4), .in5(CA5), .in6(CA6), .in7(CA7), .in8(CA8), .in9(CA9),
    .out(P2), .sel(pla_1_out));  // open: in0, in10, in11, in12, in13, in14, in15
  Multiplexer #(.select(4), .width(7)) multiplexer_2 (
    .in1(CD1), .in2(CD2), .in3(CD3), .in4(CD4), .in5(CD5), .in6(CD6), .in7(CD7), .in8(CD8), .in9(CD9),
    .out(P1), .sel(pla_2_out));  // open: in0, in10, in11, in12, in13, in14, in15
  DotMatrix dotmatrix_17 (
    .col0(ledoutput_12_out_2), .col1(ledoutput_12_out_3), .col2(ledoutput_12_out_4),
    .col3(ledoutput_12_out_5), .col4(ledoutput_12_out_6));
  LEDoutput ledoutput_12 (
    .out_2(ledoutput_12_out_2), .out_3(ledoutput_12_out_3), .out_4(ledoutput_12_out_4),
    .out_5(ledoutput_12_out_5), .out_6(ledoutput_12_out_6), .in_1(CD5));
  Button button_10 (.out(button_10_out));
  Button RESET (.out(RESET_out));
  WhoRoundWin whoroundwin_1 (.P2NUM(P2), .P1NUM(P1), .CLK(RESULT_out), .RESET(REGAME_out), .P2(SC2), .P1(SC1));
  Keyboard #(.buflen(1)) keyboard_13 (.clr(button_12_out), .data(CD6));  // open: clk, re, avail
  Keyboard #(.buflen(1)) keyboard_14 (.clr(button_11_out), .data(CA6));  // open: clk, re, avail
  Button button_11 (.out(button_11_out));
  DotMatrix dotmatrix_18 (
    .col0(ledoutput_13_out_2), .col1(ledoutput_13_out_3), .col2(ledoutput_13_out_4),
    .col3(ledoutput_13_out_5), .col4(ledoutput_13_out_6));
  LEDoutput ledoutput_13 (
    .out_2(ledoutput_13_out_2), .out_3(ledoutput_13_out_3), .out_4(ledoutput_13_out_4),
    .out_5(ledoutput_13_out_5), .out_6(ledoutput_13_out_6), .in_1(CA6));
  // Buffer buffer_1 is placed but not wired
  DotMatrix #(.matrixcols(9)) dotmatrix_19 (
    .col0(end9r_1_out_6), .col1(end9r_1_out_7), .col2(end9r_1_out_8), .col3(end9r_1_out_9),
    .col4(end9r_1_out_10), .col5(end9r_1_out_11), .col6(end9r_1_out_12), .col7(end9r_1_out_13),
    .col8(end9r_1_out_14));
  DotMatrix dotmatrix_20 (
    .col0(ledoutput_14_out_2), .col1(ledoutput_14_out_3), .col2(ledoutput_14_out_4),
    .col3(ledoutput_14_out_5), .col4(ledoutput_14_out_6));
  LEDoutput ledoutput_14 (
    .out_2(ledoutput_14_out_2), .out_3(ledoutput_14_out_3), .out_4(ledoutput_14_out_4),
    .out_5(ledoutput_14_out_5), .out_6(ledoutput_14_out_6), .in_1(CD6));
  Button button_12 (.out(button_12_out));
  // NOT_Gate not_1 has open pins: in=and_1_out, out=open
  // Buffer buffer_2 is placed but not wired
  // AND_Gate and_1 has open pins: out=and_1_out
  End9R end9r_1 (
    .P2SCORE(SC2), .E(1'b1), .CLK(RESULT_out), .P1SCORE(SC1), .RESET(REGAME_out), .out_6(end9r_1_out_6),
    .out_7(end9r_1_out_7), .out_8(end9r_1_out_8), .out_9(end9r_1_out_9), .out_10(end9r_1_out_10),
    .out_11(end9r_1_out_11), .out_12(end9r_1_out_12), .out_13(end9r_1_out_13), .out_14(end9r_1_out_14),
    .out_15(R));  // open: out_16
  Keyboard #(.buflen(1)) keyboard_15 (.clr(button_14_out), .data(CD7));  // open: clk, re, avail
  Keyboard #(.buflen(1)) keyboard_16 (.clr(button_13_out), .data(CA7));  // open: clk, re, avail
  Button button_13 (.out(button_13_out));
  DotMatrix dotmatrix_21 (
    .col0(ledoutput_15_out_2), .col1(ledoutput_15_out_3), .col2(ledoutput_15_out_4),
    .col3(ledoutput_15_out_5), .col4(ledoutput_15_out_6));
  LEDoutput ledoutput_15 (
    .out_2(ledoutput_15_out_2), .out_3(ledoutput_15_out_3), .out_4(ledoutput_15_out_4),
    .out_5(ledoutput_15_out_5), .out_6(ledoutput_15_out_6), .in_1(CA7));
  // RGB_Video #(.height(256), .scale(1), .width(256)) rgb_video_1: pin names not known; wires that end beside it: rgb_video_1_p1, rgb_video_1_p2, rgb_video_1_p3, rgb_video_1_p4, rgb_video_1_p5
  RGBmonitor rgbmonitor_1 (
    .in_2(clock_1_out), .out_6(rgb_video_1_p1), .out_7(rgb_video_1_p2), .out_3(rgb_video_1_p3),
    .out_4(rgb_video_1_p4), .out_5(rgb_video_1_p5), .in_1(1'b1));
  Clock clock_1 (.out(clock_1_out));
  DotMatrix dotmatrix_22 (
    .col0(ledoutput_16_out_2), .col1(ledoutput_16_out_3), .col2(ledoutput_16_out_4),
    .col3(ledoutput_16_out_5), .col4(ledoutput_16_out_6));
  LEDoutput ledoutput_16 (
    .out_2(ledoutput_16_out_2), .out_3(ledoutput_16_out_3), .out_4(ledoutput_16_out_4),
    .out_5(ledoutput_16_out_5), .out_6(ledoutput_16_out_6), .in_1(CD7));
  Button button_14 (.out(button_14_out));
  Keyboard #(.buflen(1)) keyboard_17 (.clr(button_16_out), .data(CD8));  // open: clk, re, avail
  Keyboard #(.buflen(1)) keyboard_18 (.clr(button_15_out), .data(CA8));  // open: clk, re, avail
  Button button_15 (.out(button_15_out));
  DotMatrix dotmatrix_23 (
    .col0(ledoutput_17_out_2), .col1(ledoutput_17_out_3), .col2(ledoutput_17_out_4),
    .col3(ledoutput_17_out_5), .col4(ledoutput_17_out_6));
  LEDoutput ledoutput_17 (
    .out_2(ledoutput_17_out_2), .out_3(ledoutput_17_out_3), .out_4(ledoutput_17_out_4),
    .out_5(ledoutput_17_out_5), .out_6(ledoutput_17_out_6), .in_1(CA8));
  DotMatrix dotmatrix_24 (
    .col0(ledoutput_18_out_2), .col1(ledoutput_18_out_3), .col2(ledoutput_18_out_4),
    .col3(ledoutput_18_out_5), .col4(ledoutput_18_out_6));
  LEDoutput ledoutput_18 (
    .out_2(ledoutput_18_out_2), .out_3(ledoutput_18_out_3), .out_4(ledoutput_18_out_4),
    .out_5(ledoutput_18_out_5), .out_6(ledoutput_18_out_6), .in_1(CD8));
  Button button_16 (.out(button_16_out));
  Keyboard #(.buflen(1)) keyboard_19 (.clr(button_18_out), .data(CD9));  // open: clk, re, avail
  Keyboard #(.buflen(1)) keyboard_20 (.clr(button_17_out), .data(CA9));  // open: clk, re, avail
  Button button_17 (.out(button_17_out));
  DotMatrix dotmatrix_25 (
    .col0(ledoutput_19_out_2), .col1(ledoutput_19_out_3), .col2(ledoutput_19_out_4),
    .col3(ledoutput_19_out_5), .col4(ledoutput_19_out_6));
  LEDoutput ledoutput_19 (
    .out_2(ledoutput_19_out_2), .out_3(ledoutput_19_out_3), .out_4(ledoutput_19_out_4),
    .out_5(ledoutput_19_out_5), .out_6(ledoutput_19_out_6), .in_1(CA9));
  DotMatrix dotmatrix_26 (
    .col0(ledoutput_20_out_2), .col1(ledoutput_20_out_3), .col2(ledoutput_20_out_4),
    .col3(ledoutput_20_out_5), .col4(ledoutput_20_out_6));
  LEDoutput ledoutput_20 (
    .out_2(ledoutput_20_out_2), .out_3(ledoutput_20_out_3), .out_4(ledoutput_20_out_4),
    .out_5(ledoutput_20_out_5), .out_6(ledoutput_20_out_6), .in_1(CD9));
  Button button_18 (.out(button_18_out));

  // Notes on the sheet:
  //   Behind of Each Card
  //   더 지니어스 : 흑과백
  //   ROUND
  //   SCORE
  //   :
  //   P1 VS P2
  //   오류판독기
  //   오류판독기
  //   P2's CARD
  //   P1's CARD
  //   WINNER
  //   모든 하얀 버튼은 리셋입니다
endmodule

module Counter4 (
  input  ENABLE,
  input  CLK,
  input  RESET,
  output [3:0] COUNT
);

  wire and_1_out, and_2_out, and_3_out;

  J_K_Flip_Flop j_k_ff_1 (.J(ENABLE), .K(ENABLE), .clk(CLK), .Q(COUNT[0]), .reset(RESET));  // open: Qn, preset
  and and_1 (and_1_out, ENABLE, COUNT[0]);
  J_K_Flip_Flop j_k_ff_2 (.J(and_1_out), .K(and_1_out), .clk(CLK), .Q(COUNT[1]), .reset(RESET));  // open: Qn, preset
  and and_2 (and_2_out, and_1_out, COUNT[1]);
  J_K_Flip_Flop j_k_ff_3 (.J(and_2_out), .K(and_2_out), .clk(CLK), .Q(COUNT[2]), .reset(RESET));  // open: Qn, preset
  and and_3 (and_3_out, and_2_out, COUNT[2]);
  J_K_Flip_Flop j_k_ff_4 (.J(and_3_out), .K(and_3_out), .clk(CLK), .Q(COUNT[3]), .reset(RESET));  // open: Qn, preset
endmodule

module LEDoutput (
  input  [6:0] in_1,
  output [6:0] out_2,
  output [6:0] out_3,
  output [6:0] out_4,
  output [6:0] out_5,
  output [6:0] out_6
);

  wire ASCTOBIN_out;

  PLA #(.in_width(4), .out_width(35), .\table ("1000 11111111000001101010110000011111111 # 8(검정)\n0111 00000000100000010000001111100000000 # 7(하양)\n0110 11111111000001101010110100011111111 # 6(검정)\n0101 00000000111010010101001011100000000 # 5(하양)\n0100 11111111000111111011110000011111111 # 4(검정)\n0011 00000000101010010101001111100000000 # 3(하양)\n0010 11111111010001101010110001011111111 # 2(검정)\n0001 00000000000000011111000000000000000 # 1(하양)\n0000 11111111000001101110110000011111111 # 0(검정)")) BINTOLED (
    .in(ASCTOBIN_out), .out({out_2, out_3, out_4, out_5, out_6}));
  PLA #(.in_width(7), .out_width(4), .\table ("0110001 0001 # 1\n0110010 0010 # 2\n0110011 0011 # 3\n0110100 0100 # 4\n0110101 0101 # 5\n0110110 0110 # 6\n0110111 0111 # 7\n0111000 1000 # 8\n0110000 0000 # 0")) ASCTOBIN (
    .in(in_1), .out(ASCTOBIN_out));
endmodule

module COVERoutput (
  input  [6:0] in_1,
  output [4:0] out_2,
  output [4:0] out_3,
  output [4:0] out_4
);

  PLA #(.in_width(7), .out_width(15), .\table ("0110001 000000000000000 # 1\n0110010 111111111111111 # 2\n0110011 000000000000000 # 3\n0110100 111111111111111 # 4\n0110101 000000000000000 # 5\n0110110 111111111111111 # 6\n0110111 000000000000000 # 7\n0111000 111111111111111 # 8\n0110000 111111111111111 # 0")) COVER (
    .in(in_1), .out({out_2, out_3, out_4}));
endmodule

module Alladder (
  input  [6:0] in_1,
  input  [6:0] in_2,
  input  [6:0] in_3,
  input  [6:0] in_4,
  input  [6:0] in_5,
  input  [6:0] in_6,
  input  [6:0] in_7,
  input  [6:0] in_8,
  input  [6:0] in_9,
  output [6:0] out_10,
  output [6:0] out_11,
  output [6:0] out_12,
  output [6:0] out_13,
  output [6:0] out_14,
  output [6:0] out_15,
  output [6:0] out_16,
  output [6:0] out_17,
  output [6:0] out_18
);

  wire [6:0] adder_1_out, adder_2_out, adder_3_out, adder_4_out, adder_5_out, adder_6_out, adder_7_out,
       adder_8_out;

  Adder #(.width(7)) adder_1 (.a(in_1), .b(in_2), .out(adder_1_out));  // open: cin, cout
  Adder #(.width(7)) adder_2 (.a(in_3), .b(in_4), .out(adder_2_out));  // open: cin, cout
  Adder #(.width(7)) adder_3 (.a(in_5), .b(in_6), .out(adder_3_out));  // open: cin, cout
  Adder #(.width(7)) adder_4 (.a(in_7), .b(in_8), .out(adder_4_out));  // open: cin, cout
  Adder #(.width(7)) adder_5 (.a(adder_1_out), .b(adder_2_out), .out(adder_5_out));  // open: cin, cout
  Adder #(.width(7)) adder_6 (.a(adder_3_out), .b(adder_4_out), .out(adder_6_out));  // open: cin, cout
  Adder #(.width(7)) adder_7 (.a(adder_5_out), .b(adder_6_out), .out(adder_7_out));  // open: cin, cout
  Adder #(.width(7)) adder_8 (.a(adder_7_out), .b(in_9), .out(adder_8_out));  // open: cin, cout
  PLA #(.in_width(7), .out_width(63), .\table ("1010100 000000001111100001010000111000000000111110000101000011100000000 # 굿\nxxxxxxx 001110000101000111110000100000000000001100001000000011000111110 # 다시.")) ERROR (
    .in(adder_8_out), .out({out_10, out_11, out_12, out_13, out_14, out_15, out_16, out_17, out_18}));
endmodule

module WhoRoundWin (
  input  [6:0] P2NUM,
  input  [6:0] P1NUM,
  input  CLK,
  input  RESET,
  output [3:0] P2,
  output [3:0] P1
);

  wire comparator_1_gt, comparator_1_lt;

  Comparator #(.mode("unsigned"), .width(7)) comparator_1 (
    .a(P2NUM), .b(P1NUM), .gt(comparator_1_gt), .lt(comparator_1_lt));  // open: eq
  Counter4 counter4_1 (.ENABLE(comparator_1_gt), .CLK(CLK), .RESET(RESET), .COUNT(P2));
  Counter4 counter4_2 (.ENABLE(comparator_1_lt), .CLK(CLK), .RESET(RESET), .COUNT(P1));
endmodule

module End9R (
  input  [3:0] P2SCORE,
  input  E,
  input  CLK,
  input  [3:0] P1SCORE,
  input  RESET,
  output [6:0] out_6,
  output [6:0] out_7,
  output [6:0] out_8,
  output [6:0] out_9,
  output [6:0] out_10,
  output [6:0] out_11,
  output [6:0] out_12,
  output [6:0] out_13,
  output [6:0] out_14,
  output [3:0] out_15,
  output [4:0] out_16
);

  wire and_1_out, comparator_1_gt, comparator_1_lt, or_1_out, or_2_out;
  wire [3:0] controlled_buffer_1_out, controlled_buffer_2_out;

  Counter4 counter4_1 (.ENABLE(E), .CLK(CLK), .RESET(RESET), .COUNT(out_15));
  and and_1 (and_1_out, out_15[0], out_15[3]);
  or or_1 (or_1_out, out_16[0], out_16[4]);
  or or_2 (or_2_out, and_1_out, or_1_out);
  assign controlled_buffer_1_out = or_2_out ? P2SCORE : 4'bz;  // Controlled_Buffer controlled_buffer_1
  assign controlled_buffer_2_out = or_2_out ? P1SCORE : 4'bz;  // Controlled_Buffer controlled_buffer_2
  Comparator #(.mode("unsigned"), .width(4)) comparator_1 (
    .a(controlled_buffer_1_out), .b(controlled_buffer_2_out), .gt(comparator_1_gt), .eq(out_16[2]),
    .lt(comparator_1_lt));
  Comparator #(.mode("unsigned"), .width(4)) comparator_2 (.a(P2SCORE), .b(4'b0101), .eq(out_16[0]));  // open: gt, lt
  Comparator #(.mode("unsigned"), .width(4)) comparator_3 (.a(P1SCORE), .b(4'b0101), .eq(out_16[4]));  // open: gt, lt
  and and_2 (out_16[1], comparator_1_gt, 1'b1);
  and and_3 (out_16[3], 1'b1, comparator_1_lt);
  PLA #(.in_width(5), .out_width(63), .\table ("00010 000000001111100101000011100000000000101110010101001110100000000 # P2W\n01000 000000001111100101000011100000000000010010011111000000100000000 # P1W\n00000 000000000000000000000000000000000000000000000000000000000000000 # NO\n00100 000000001111100101000001111000000000011100010101001010100000000 # DRAW\n0xxx1 000000001111100101000011100000000000101110010101001110100000000 # P2W\n1xxx0 000000001111100101000011100000000000010010011111000000100000000 # P1W")) WHOWIN (
    .in(out_16), .out({out_6, out_7, out_8, out_9, out_10, out_11, out_12, out_13, out_14}));

  // Other names for the same wires on the sheet: P2W = out_16[0]; P1W = out_16[4]
endmodule

module RGBmonitor (
  input  in_1,
  input  in_2,
  output [7:0] out_3,
  output [7:0] out_4,
  output [15:0] out_5,
  output out_6,
  output out_7
);

  wire counter_1_carry;

  Counter counter_1 (.count(in_1), .clk(in_2), .carry(counter_1_carry), .Q(out_3));  // open: clr, load, up, D
  Counter counter_2 (.count(in_1), .clk(counter_1_carry), .Q(out_4));  // open: clr, load, up, D, carry
  ROM #(.addrWidth(16), .dataWidth(16)) rom_1 (.addr({out_4, out_3}), .data(out_5));

  assign out_6 = in_2;
  assign out_7 = in_1;

  // Notes on the sheet:
  //   contents of rom_1 (hex, n*v repeats v):
  //   2881 2861 2881 5*3061 4*3081 30a1 4*3081 30a1 30a1 3081 3081 30a1 30a1 30a1 30a2 7*30a1 38c2 30c2
  //   30c2 12*38c2 4*38e2 38e3 4*38e2 3903 3903 3903 38e2 38e3 38e3 40e3 40e3 40e2 40e2 5*3903 4103 3903
  //   5*4103 3923 3923 3903 14*4103 3903 24*4103 40e3 4103 40e3 4903 4103 4103 4103 4124 4104 4104 4103
  //   4103 4904 6*40e3 7*4103 4123 4103 4103 4103 3903 18*4103 4104 4103 4104 4103 4104 4103 4103 4103
  //   4104 4104 4104 48e4 40e4 40e4 4104 4104 3904 4104 4103 4103 4103 40e3 4903 40e3 4103 4103 4103 3903
  //   38e2 38e2 38e2 3903 38e2 38e2 38e2 40e2 38e2 38e3 38e3 38e2 38e2 38c2 38c2 38e2 38e2 7*38c2 30c2
  //   30c2 30c2 38c2 38c2 30a2 30a2 30a2 30a1 30a1 30a2 3081 30a1 30a2 30a1 11*3081 2881 3061 3060 3061
  //   3061 3041 2861 2881 2081 2881 2881 2881 3081 4*3061 3081 3081 3081 3061 3081 3081 3061 6*3081 30a1
  //   38a2 30a1 3081 3081 3081 30a1 3881 3081 3081 3881 38a2 38a1 38a2 38c1 38c2 38a1 38a2 38c2 38a2
  //   10*38c2 4*40c2 40e2 38c2 4*38e2 40e2 40e3 40e3 40e2 40e2 40e2 38e2 38e2 40e3 4103 4103 5*40e3 40e2
  //   4103 4103 4102 25*4103 40e3 4*4103 40e3 7*4103 48e3 4103 4903 40e3 4903 40e3 4103 38e3 38e3 4*4103
  //   40e3 48e3 4904 4903 5*40e3 4103 4103 4903 13*4103 40e2 40e3 4103 4103 4103 9*40e3 4103 40e3 4103
  //   10*40e3 4104 40e3 40e3 4103 4103 4103 40e3 40e3 40e2 40e2 40e3 40e2 40e3 40e2 40e2 38e2 4*40e2 40c2
  //   40c2 40c2 40e2 4*38c2 40c2 6*38c2 38c1 38a2 38c1 38a2 38a2 38a2 38a1 3882 38a1 3882 3881 3881 38a1
  //   3881 3881 3881 9*3081 5*3061 3060 4*3061 2881 2881 2861 2861 3061 3061 3061 4*3861 3081 3061 3081
  //   3881 3881 3061 8*3881 3861 3881 3881 4081 40a1 4081 4081 4081 40a2 4081 40a1 4081 40a1 40a2 40a1
  //   7*40a2 40c2 48c2 48c2 40c2 48c2 48c2 48c2 48a2 48c2 48a2 48c2 48c2 40c2 40e2 40e2 40e2 48e2 48c2
  //   48c2 48e3 48e2 48e2 48c2 48c2 48e3 48e3 48e3 5103 5103 48e3 48e3 48e3 7*4903 11*48e3 48e2 11*48e3
  //   48e2 40e3 40e3 40e3 40c2 4*40e3 40e2 40e2 40c2 40e2 40e2 40e2 40a2 40c2 40e3 4123 4123 5*4103 40c3
  //   40c2 40c3 40c2 40e3 48e3 48c3 40c2 40e3 40e3 48e3 48e3 40e2 40e2 48c2 48e2 48e3 48e3 48e3 48e2 48c2
  //   48e3 48e3 4903 48e3 48e3 5103 5103 50e3 4*4903 4*48e3 4903 48e3 5103 4903 5103 4903 5103 5103 8*4903
  //   48e3 48e3 48e3 4903 4903 4902 48e2 48e3 48e2 48c2 48e2 48e3 48e3 48e3 48e2 48e3 48e2 48e3 48c2 48c2
  //   48c2 40c2 6*48c2 40c2 40a2 40c2 40a2 40c2 7*40a2 40a1 40a2 40a1 40a2 3881 3881 3881 40a2 4081 4*3881
  //   3861 3061 3081 3881 3881 3861 3061 3060 3060 3081 3060 4*3040 2861 2881 2861 2861 2861 3061 3061
  //   3861 3861 3861 4081 3881 3881 3861 38a2 3882 40a2 3881 40a2 48a2 48c2 50c3 50e3 50e3 5103 50e3 50e3
  //   50e3 5103 5924 5923 5924 5923 5924 5944 4*6144 6165 6164 4*6165 6185 6165 6165 6985 6985 6985 69a6
  //   6986 6986 6985 6985 6965 6965 6985 6985 6985 61a5 61a5 69a6 61a6 4*6985 6986 69a6 6986 6986 6986
  //   6985 6985 6985 6965 9*6165 6145 6144 6144 6144 5944 5944 5924 5944 4*5924 5903 4*5103 50e3 50e3 50e3
  //   48c2 48c2 48a2 40a2 40a2 4081 4081 5*3861 3060 3040 3040 3840 3040 3040 3000 3020 3061 40e3 5*4103
  //   40e3 3881 3861 3881 3861 3881 3881 3861 3861 3881 38a1 4082 4081 48c2 48c2 48c2 50e2 5103 5103 5103
  //   50e3 50c2 50e3 5903 5903 5903 5924 6124 6124 4*6144 5*6164 6165 6164 6185 6164 5*6985 6185 6185 61a5
  //   61a5 6185 6185 69a6 6985 6185 6985 69a5 61a5 61a5 61a5 69a6 69a5 6986 10*69a6 6985 6985 69a5 6985
  //   6985 6986 6985 6985 6165 6165 6185 6165 6144 6144 6144 5944 5944 6*5924 5904 5103 5103 5103 50e3
  //   50e3 48c3 48c2 48c2 40a2 40a2 4081 3861 3881 3881 3861 3861 3061 3061 3060 3861 3040 3020 3020 3020
  //   2840 2861 2861 3061 2861 3061 3061 3861 3841 3841 3841 4061 3861 3861 4081 4081 40a2 4081 48a2 48a2
  //   50a2 50c3 58e3 58e3 5903 58e3 50c2 50c2 5903 5903 6103 6104 6124 6124 6144 6944 6*6144 6944 6144
  //   6965 6965 6964 6945 6965 6965 6965 5*6985 8*6965 7185 7165 6965 7*6985 6965 4*7185 7165 7*6965 6945
  //   6144 6144 6144 8*6124 5*5903 58e3 4*50e3 50c2 48c2 48a2 4881 4081 4061 4061 3861 4061 3861 3861 3860
  //   3840 3840 3860 3040 3020 3020 3061 6*4103 40e3 3861 3840 3840 3840 3861 4061 4041 3840 4061 4081
  //   4081 4081 48a2 48a1 50a2 50c2 5903 58e3 5903 58e3 58c3 58e3 5903 5903 6104 6124 6944 6944 6144 6944
  //   6944 6944 6144 6*6964 6985 6964 6985 6964 8*6985 7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
endmodule
